# Fritzing sketch GPIO_listener (saved by Fritzing 0.9.3b)

parts:
  Raspberry_Pi2/3/4 = Raspberry Pi B+
  4 = Pushbutton [package=THT]
  1 = Pushbutton [package=THT]
  5 = Pushbutton [package=THT]
  25 = Pushbutton [package=THT]
  24 = Pushbutton [package=THT]
  6 = Pushbutton [package=THT]
  23 = Pushbutton [package=THT]
  28 = Pushbutton [package=THT]
  21 = Pushbutton [package=THT]
  26 = Pushbutton [package=THT]
  22 = Pushbutton [package=THT]
  29 = Pushbutton [package=THT]
  S2 = Round Pushbutton
  LED1 = smd LED [color="Green (565nm)" package="1206 [SMD]"]

nets:
  N1: Raspberry_Pi2/3/4.GPIO3, S2.leg0
  N2: Raspberry_Pi2/3/4.GND, 4.leg1, 1.leg1, 5.leg1, 25.leg1, 24.leg1, 6.leg1, 23.leg1, 28.leg1, 21.leg1, 26.leg1, 22.leg1, 29.leg1, S2.leg1
  N3: Raspberry_Pi2/3/4.GPIO27, LED1.anode
  N4: Raspberry_Pi2/3/4.GPIO5, 21.leg0
  N5: Raspberry_Pi2/3/4.GPIO6, 22.leg0
  N6: Raspberry_Pi2/3/4.GPIO13, 23.leg0
  N7: Raspberry_Pi2/3/4.GPIO19, 24.leg0
  N8: Raspberry_Pi2/3/4.GPIO26, 25.leg0
  N9: Raspberry_Pi2/3/4.GPIO21, 29.leg0
  N10: Raspberry_Pi2/3/4.GPIO20, 28.leg0
  N11: Raspberry_Pi2/3/4.GPIO12, 26.leg0
  N12: Raspberry_Pi2/3/4.GPIO25, 6.leg0
  N13: Raspberry_Pi2/3/4.GPIO24, 5.leg0
  N14: Raspberry_Pi2/3/4.GPIO23, 4.leg0
  N15: Raspberry_Pi2/3/4.GPIO18, 1.leg0

notes:
  Buttons' detection (wPi) numbers.
  Açma kapama butonu
  Sadece rPi4'de geçerlidir.
  HDD Led
  Disk aktivitesini göre yanar. Etkinleştirmek için /boot/config.txt düzenlenir.
